# Fritzing sketch CicadaPCB (saved by Fritzing 0.9.3b)
breadboards: 3

parts:
  LM1 = LM2596 [package=TO-220F-5L]
  Power_plug2 = Power plug [part_number=Battery]
  D1 = Schottky Diode [part_number=1N5824 package="300 mil [THT]"]
  D2 = Schottky Diode [part_number=1N5824 package="300 mil [THT]"]
  R1 = Resistor [tolerance=±5% resistance=1k package=THT]
  Power_plug3 = Power plug [part_number=PowerSupply]
  LED1 = LED - 5mm [color="Red (633nm)" part_number="Led Power Supply" package="5 mm [THT]"]
  D3 = Schottky Diode [part_number=1N5824 package="300 mil [THT]"]
  C6 = Electrolytic Capacitor [capacitance=1000µF voltage=25V part_number=680uF package="200 mil [THT, electrolytic]"]
  L1 = Inductor [inductance=33µH package="400 mil [THT]"]
  C7 = Electrolytic Capacitor [capacitance=0.22mF voltage=25V part_number=220uF package="200 mil [THT, electrolytic]"]
  D4 = Schottky Diode [part_number=1N5824 package="300 mil [THT]"]
  SIM800L1 = SIM800L
  Q2 = Basic FET N-Channel [part_number=IRF540N package="TO220 [THT]"]
  U1 = Sharp PC817 [package=THT]
  R2 = Resistor [tolerance=±5% resistance=1k package=THT]
  R4 = Resistor [tolerance=±5% resistance=39k package=THT]
  R3 = Resistor [tolerance=±5% resistance=1k package=THT]
  LED2 = LED - 5mm [color="Red (633nm)" package="5 mm [THT]"]
  LED3 = LED - 5mm [color="Green (555nm)" package="5 mm [THT]"]
  LED4 = LED - 5mm [color="Blue (430nm)" package="5 mm [THT]"]
  R5 = Resistor [tolerance=±5% resistance=1k package=THT]
  R6 = Resistor [tolerance=±5% resistance=1k package=THT]
  R7 = Resistor [tolerance=±5% resistance=1k package=THT]
  S1 = Pushbutton [part_number="Enable Wizard" package="[THT]"]
  R8 = Resistor [tolerance=±5% resistance=1k package=THT]
  D5 = Schottky Diode [part_number=1N4004 package="300 mil [THT]"]
  J9 = Screw terminal - 2 pins [part_number="Rain Gauge ReedSwith" package=THT]
  R9 = Resistor [tolerance=±5% resistance=1k package=THT]
  R10 = Resistor [tolerance=±5% resistance=33k package=THT]
  R11 = Resistor [tolerance=±5% resistance=10k package=THT]
  C8 = Capacitor [part_number=100nF package=cap-pth-small2]
  R12 = Resistor [tolerance=±5% resistance=10k package=THT]  # not connected
  R13 = Resistor [tolerance=±5% resistance=33k package=THT]
  J10 = Screw terminal - 2 pins [part_number="Solar cell voltage" package=THT]  # not connected
  C9 = Capacitor [part_number=100nF package=cap-pth-small2]
  J11 = screw terminal, 3 pins [part_number="DHT 22"]
  R14 = Resistor [tolerance=±5% resistance=1k package=THT]
  microSD1 = MicroSD Card Module
  ESP32_DEVKIT1 = ESP32 DEVKIT 38 pins

nets:
  N1: LM1.VIN, D1.cathode, D2.cathode, C6.+
  N2: LM1.VOUT, D3.cathode, L1.pin_1
  GND: LM1.GND, LM1.ON/OFF, Power_plug2.GND, Power_plug3.GND, LED1.cathode, D3.anode, C6.-, C7.-, Q2.source, U1.Pin_1, R4.Pin_0, LED2.cathode, LED3.cathode, LED4.cathode, R8.Pin_1, R11.Pin_1, C8.2, C9.2, J11.pin3, microSD1.GND, ESP32_DEVKIT1.GND#64
  N3: LM1.FEED, L1.pin_0, C7.+, D4.anode, D5.anode, R9.Pin_1
  N4: Power_plug2.VCC, D1.anode, R10.Pin_0
  N5: D2.anode, R1.Pin_0, Power_plug3.VCC
  N6: R1.Pin_1, LED1.anode
  N7: D4.cathode, SIM800L1.VCC
  N8: SIM800L1.RXD, ESP32_DEVKIT1.IO16
  N9: SIM800L1.TXD, ESP32_DEVKIT1.IO17
  N10: SIM800L1.GND, Q2.drain
  N11: Q2.gate, R2.Pin_0, R4.Pin_1
  N12: U1.Pin_2, R3.Pin_0
  N13: U1.Pin_4, D5.cathode, J11.pin1, R14.Pin_0, ESP32_DEVKIT1.5V
  N14: U1.Pin_3, R2.Pin_1
  N15: R3.Pin_1, ESP32_DEVKIT1.IO23
  N16: LED2.anode, R7.Pin_0
  N17: LED3.anode, R6.Pin_0
  N18: LED4.anode, R5.Pin_0
  N19: R5.Pin_1, ESP32_DEVKIT1.IO25
  N20: R6.Pin_1, ESP32_DEVKIT1.IO33
  N21: R7.Pin_1, ESP32_DEVKIT1.IO32
  N22: S1.Pin_1, S1.Pin_2, R8.Pin_0, ESP32_DEVKIT1.IO26
  VCC: S1.Pin_3, S1.Pin_4, J9.pin1, microSD1.VCC, ESP32_DEVKIT1.3V3
  N23: J9.pin2, R9.Pin_0, ESP32_DEVKIT1.IO4
  N24: R10.Pin_1, R11.Pin_0, C8.1, ESP32_DEVKIT1.IO35
  N25: R13.Pin_1, C9.1, ESP32_DEVKIT1.IO34
  N26: J11.pin2, R14.Pin_1, ESP32_DEVKIT1.IO14
  N27: microSD1.MISO, ESP32_DEVKIT1.IO18
  N28: microSD1.MOSI, ESP32_DEVKIT1.IO19
  N29: microSD1.SCK, ESP32_DEVKIT1.IO22
  N30: microSD1.CS, ESP32_DEVKIT1.IO21

custom parts:
  LM2596: Regulator is a DC linear voltage regulator which can operate with a very small input–output differential voltage. The advantages of a low dropout voltage include a lower minimum operating voltage, higher efficiency operation and lower heat dissipation.
  SIM800L: SIM800L is a miniature cellular module which allows for GPRS transmission, sending and receiving SMS and making and receiving voice calls. Low cost and small footprint and quad band frequency support make this module perfect solution for any project that require long range connectivity. After connecting power module boots up, searches for cellular network and login automatically. On board LED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
